# Fritzing sketch protest sign (saved by Fritzing 0.9.2b)

parts:
  SW1 = DIP Switch 8 Position [package=dipswitch-08]  # not connected
  R1 = Resistor [tolerance=±5% resistance=10k package=THT]  # not connected
  R2 = Resistor [tolerance=±5% resistance=10k package=THT]  # not connected
  R3 = Resistor [tolerance=±5% resistance=10k package=THT]  # not connected
  R4 = Resistor [tolerance=±5% resistance=10k package=THT]  # not connected
  R5 = Resistor [tolerance=±5% resistance=10k package=THT]  # not connected
  R6 = Resistor [tolerance=±5% resistance=10k package=THT]  # not connected
  R7 = Resistor [tolerance=±5% resistance=10k package=THT]  # not connected
  R8 = Resistor [tolerance=±5% resistance=10k package=THT]  # not connected
  proto1 = Adafruit_PermaProto_1_4_Board
  C1 = Electrolytic Capacitor [capacitance=1µF package="100 mil [THT, electrolytic]"]  # not connected
  R9 = Resistor [tolerance=±5% resistance=470 package=THT]  # not connected
  Part1 = Adafruit Feather M0 Adalogger [part_number="Adafruit #2796"]
  NEOPIXEL2 = Neopixel Strip -- White (30/m)
  BATT1 = LiPoly Battery (1300mAh)  # not connected

nets:
  N1: proto1.connectorD3, Part1.D5
  N2: proto1.connectorD4, Part1.D9
  N3: proto1.connectorD5, Part1.D10
  N4: proto1.connectorD6, Part1.D11
  N5: proto1.connectorD7, Part1.D12
  N6: proto1.connectorD8, Part1.D13
  N7: proto1.connectorD9, Part1.A1
  N8: proto1.connectorD10, Part1.A0
  N9: proto1.connectorD13, Part1.D6
  N10: proto1.connectorH3, proto1.connectorY3
  N11: proto1.connectorH4, proto1.connectorY4
  N12: proto1.connectorH5, proto1.connectorY5
  N13: proto1.connectorH6, proto1.connectorY6
  N14: proto1.connectorH7, proto1.connectorY7
  N15: proto1.connectorH8, proto1.connectorY8
  N16: proto1.connectorH9, proto1.connectorY9
  N17: proto1.connectorH10, proto1.connectorY10
  N18: proto1.connectorJ13, NEOPIXEL2.Din
  N19: proto1.connectorX12, proto1.connectorZ12
  N20: proto1.connectorY1, Part1.VBAT
  N21: proto1.connectorY13, NEOPIXEL2.+5V
  N22: proto1.connectorZ1, Part1.GND
  N23: proto1.connectorZ13, NEOPIXEL2.GND

custom parts:
  Adafruit Feather M0 Adalogger: This is the Adafruit Feather M0 Adalogger - our take on an 'all-in-one' Cortex M0 datalogger (or data-reader) with built in USB and battery charging. Its an Adafruit Feather M0 with a microSD holder ready to rock! We have other boards in the Feather family, check'em out here At the Feather M0's heart is an ATSAMD21G18 ARM Cortex M0 processor, clocked at 48 MHz and at 3.3V logic, the same one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
  Neopixel Strip -- White (30/m): These NeoPixel strips have 30 digitally-addressable pixel LEDs per meter and are very affordable and are only 12.5 mm wide, 10 mm if you remove the strip from the casing.
  LiPoly Battery (1300mAh): Lithium Ion Polymer Battery (1300mAh)
